# Fritzing sketch Arduino_L298N_Motor (saved by Fritzing 0.9.3b)

parts:
  Part1 = Arduino Uno (Rev3)
  S1 = H-Bridge with L298N
  DC_Mot_Enc1 = DC Motor with two-phase hall-encoder [part_number=VT-E-G25A-06-177E]
  VCC1 = Battery

nets:
  N1: Part1.D8, S1.IN2
  N2: Part1.D10_PWM/SS, S1.ENA
  N3: Part1.D3_PWM, DC_Mot_Enc1.pin3
  N4: Part1.D4, DC_Mot_Enc1.pin4
  N5: Part1.GND, DC_Mot_Enc1.pin2, VCC1.-
  N6: S1.12V, VCC1.+
  N7: S1.M1-01, DC_Mot_Enc1.pin6
  N8: S1.M1-02, DC_Mot_Enc1.pin1

notes:
  Motor Wiring:
  -------------------
  White - Motor -Ve
  Blue - Encoder +Ve
  Green - Encoder B
  Yellow - Encoder A
  Black - Encoder -Ve
  Red - Motor +Ve
  12V Power Supply

custom parts:
  H-Bridge with L298N: h-bridge
